// Digital circuit ROOT.dig as structural Verilog
module ROOT (
);

  wire if_1_p1;

  ID id_1 ();
  // IF if_1: pin names not known; wires that end beside it: if_1_p1
  // IFIDReg ifidreg_1: pin names not known; wires that end beside it: if_1_p1
  IF if_2 ();  // open: PC1, _1, _2, _444
endmodule
